# Fritzing sketch tedx_master_schematic (saved by Fritzing 0.8.3b)
breadboards: 1

parts:
  Part1 = Arduino Uno (Rev3)
  LED1 = RGB LED (com. cathode, rbg) [package="5 mm [THT]"]
  R1 = Resistor [tolerance=±5% resistance=220 package=THT]
  R2 = Resistor [tolerance=±5% resistance=220 package=THT]
  R3 = Resistor [tolerance=±5% resistance=220 package=THT]
  R4 = Rotary Potentiometer (Small)

nets:
  N1: Part1.GND, LED1.common_cathode, R4.leg1
  N2: Part1.D3_PWM, R1.Pin_1
  N3: Part1.D5_PWM, R2.Pin_1
  N4: Part1.D6_PWM, R3.Pin_1
  N5: Part1.5V, R4.leg2
  N6: LED1.red_anode, R3.Pin_0
  N7: LED1.blue_anode, R2.Pin_0
  N8: LED1.green_anode, R1.Pin_0

notes:
  Connect input to output of other circuit, and vice versa.
